# Fritzing sketch biocontrolador (saved by Fritzing 0.7.12b)
breadboards: 1

parts:
  part = Arduino Nano v2.3
  Sensor_Luz = double row male pin header, 2 pins [form="♂ (male)"]
  Sensor_Suelo = female pin header, 4 pins [form="♀ (female)"]  # not connected
  Power_plug1 = Power plug
  Reles = male pin header, 4 pins [form="♂ (male)"]
  R1 = Photocell (LDR) [package=THT]
  R2 = Resistor [tolerance=±5% resistance=220 package=THT]  # not connected
  Led_Rojo = female pin header, 2 pins [form="♀ (female)"]  # not connected
  Led_Verde = female pin header, 2 pins [form="♀ (female)"]  # not connected

nets:
  GND: part.GND, Power_plug1.GND
  VIN: part.VIN, Power_plug1.VCC, Reles.pin4
  N1: Sensor_Luz.pin1, R1.pin_0
  N2: Sensor_Luz.pin2, R1.pin_1
