# Fritzing sketch biocontrolador1 (saved by Fritzing 0.7.11b)
breadboards: 1

parts:
  Nano1 = Arduino Nano v2.3
  Sensor_Luz = double row male pin header, 2 pins [form="♂ (male)"]
  Sensor_Suelo = female pin header, 4 pins [form="♀ (female)"]  # not connected
  Power_plug1 = Power plug
  Reles = male pin header, 4 pins [form="♂ (male)"]
  R2 = Resistor [tolerance=±5% resistance=220 package=THT]
  Led_Rojo = female pin header, 2 pins [form="♀ (female)"]  # not connected
  Led_Verde = female pin header, 2 pins [form="♀ (female)"]  # not connected
  Led_verde = female pin header, 2 pins [form="♀ (female)"]  # not connected

nets:
  GND: Nano1.GND, Power_plug1.GND, R2.Pin_1
  N1: Nano1.D12, Reles.pin4
  N2: Nano1.A7, Sensor_Luz.pin2, R2.Pin_0
  VIN: Nano1.VIN, Sensor_Luz.pin1, Power_plug1.VCC
